# Fritzing sketch nodemcu-bot (saved by Fritzing 0.9.4)
breadboards: 1

parts:
  Part2 = BME280 Breakout
  R1 = Resistor [tolerance=±5% resistance=10k package=THT]
  R2 = Resistor [tolerance=±5% resistance=10k package=THT]
  OLED_I2C1 = OLED 128x64 I2C Monochrome Display
  U1 = NodeMCU V3.0 [part_number="Lolin v0.1"]

nets:
  GND: Part2.GND, OLED_I2C1.GND, U1.GND
  3.3V: Part2.3.3V, R1.Pin_0, R2.Pin_0, OLED_I2C1.VDD, U1.3V3
  N1: Part2.SDI/SDA, R1.Pin_1, OLED_I2C1.SDA, U1.D2
  N2: Part2.SCK/SCL, R2.Pin_1, OLED_I2C1.SCK, U1.D1

notes:
  Bus i2C
  3V3   GND
  SDA   SCL

custom parts:
  NodeMCU V3.0: ESP8266 based NodeMCU
